// Logisim project PSG.circ as structural Verilog: 2 circuits, main circuit main
module main (
  input  D0,
  input  D1,
  input  D2,
  input  D3,
  input  D4,
  input  D5,
  input  D6,
  input  D7,
  input  D8,
  input  D9,
  input  D10,
  input  D11,
  input  D12,
  input  D13,
  input  D14,
  input  D15,
  output D0_2,
  output D1_2,
  output D2_2,
  output D3_2,
  output D4_2,
  output D5_2,
  output D6_2,
  output D7_2,
  output D8_2,
  output D9_2,
  output D10_2,
  output D11_2,
  output D12_2,
  output D13_2,
  output D14_2,
  output D15_2,
  output out_33,
  output out_34,
  output out_35,
  output [7:0] DAC0,
  output out_37,
  output out_38,
  output out_39,
  output [7:0] DAC1,
  output out_41,
  output out_42,
  output out_43,
  output [7:0] DAC2,
  output out_45,
  output out_46,
  output out_47,
  output [7:0] DAC3,
  output [3:0] out_49
);

  wire and_1_out, and_2_out, and_3_out, and_4_out, d_latch_1_q, d_latch_2_q, d_latch_3_q, d_latch_4_q,
       d_latch_5_q, d_latch_6_q, d_latch_7_q, d_latch_8_q, d_latch_9_q, d_latch_10_q, d_latch_11_q,
       d_latch_12_q, d_latch_13_q, d_latch_14_q, d_latch_15_q, d_latch_16_q, d_latch_17_q, d_latch_18_q,
       d_latch_19_q, d_latch_20_q, nor_1_out, nor_2_out, nor_3_out, nor_4_out, not_1_out, not_2_out,
       not_3_out, not_4_out, not_5_out, not_6_out, not_7_out, not_8_out, not_9_out, or_1_out, or_2_out,
       or_3_out, or_4_out, or_8_out, or_12_out, or_16_out, or_20_out, undriven, undriven_2, undriven_3,
       undriven_4, undriven_5, undriven_6, undriven_7, undriven_8, undriven_9, undriven_10, undriven_11,
       undriven_12, undriven_13, undriven_14, undriven_15, undriven_16, undriven_18, undriven_19;
  wire [1:0] undriven_17;
  wire [2:0] or_5_out, or_9_out, or_13_out, or_17_out;

  D_LATCH d_latch_1 (.EN(undriven), .D(undriven_2), .Q(d_latch_1_q));  // open: nQ
  D_LATCH d_latch_2 (.EN(undriven), .D(undriven_3), .Q(d_latch_2_q));  // open: nQ
  D_LATCH d_latch_3 (.EN(undriven), .D(undriven_4), .Q(d_latch_3_q));  // open: nQ
  D_LATCH d_latch_4 (.EN(undriven), .D(undriven_5), .Q(d_latch_4_q));  // open: nQ
  and and_1 (and_1_out, d_latch_1_q, undriven_6);
  and and_2 (and_2_out, d_latch_2_q, undriven_6);
  and and_3 (and_3_out, d_latch_3_q, undriven_6);
  and and_4 (and_4_out, d_latch_4_q, undriven_6);
  not not_1 (not_1_out, undriven_6);
  not not_2 (not_2_out, undriven_7);
  not not_3 (not_3_out, undriven_8);
  not not_4 (not_4_out, undriven_9);
  not not_5 (not_5_out, undriven_10);
  or or_1 (or_1_out, and_1_out, not_1_out);
  or or_2 (or_2_out, and_2_out, not_1_out);
  or or_3 (or_3_out, and_3_out, not_1_out);
  or or_4 (or_4_out, and_4_out, not_1_out);
  D_LATCH d_latch_5 (.EN(not_2_out), .D(or_1_out), .Q(d_latch_5_q));  // open: nQ
  D_LATCH d_latch_6 (.EN(not_2_out), .D(or_2_out), .Q(d_latch_6_q));  // open: nQ
  D_LATCH d_latch_7 (.EN(not_2_out), .D(or_3_out), .Q(d_latch_7_q));  // open: nQ
  D_LATCH d_latch_8 (.EN(not_2_out), .D(or_4_out), .Q(d_latch_8_q));  // open: nQ
  D_LATCH d_latch_9 (.EN(not_3_out), .D(or_1_out), .Q(d_latch_9_q));  // open: nQ
  D_LATCH d_latch_10 (.EN(not_3_out), .D(or_2_out), .Q(d_latch_10_q));  // open: nQ
  D_LATCH d_latch_11 (.EN(not_3_out), .D(or_3_out), .Q(d_latch_11_q));  // open: nQ
  D_LATCH d_latch_12 (.EN(not_3_out), .D(or_4_out), .Q(d_latch_12_q));  // open: nQ
  D_LATCH d_latch_13 (.EN(not_4_out), .D(or_1_out), .Q(d_latch_13_q));  // open: nQ
  D_LATCH d_latch_14 (.EN(not_4_out), .D(or_2_out), .Q(d_latch_14_q));  // open: nQ
  D_LATCH d_latch_15 (.EN(not_4_out), .D(or_3_out), .Q(d_latch_15_q));  // open: nQ
  D_LATCH d_latch_16 (.EN(not_4_out), .D(or_4_out), .Q(d_latch_16_q));  // open: nQ
  D_LATCH d_latch_17 (.EN(not_5_out), .D(or_1_out), .Q(d_latch_17_q));  // open: nQ
  D_LATCH d_latch_18 (.EN(not_5_out), .D(or_2_out), .Q(d_latch_18_q));  // open: nQ
  D_LATCH d_latch_19 (.EN(not_5_out), .D(or_3_out), .Q(d_latch_19_q));  // open: nQ
  D_LATCH d_latch_20 (.EN(not_5_out), .D(or_4_out), .Q(d_latch_20_q));  // open: nQ
  nor nor_1 (nor_1_out, undriven_11, undriven_15);
  nor nor_2 (nor_2_out, undriven_12, undriven_15);
  nor nor_3 (nor_3_out, undriven_13, undriven_15);
  nor nor_4 (nor_4_out, undriven_14, undriven_15);
  or or_5 (or_5_out[0], d_latch_5_q, nor_1_out);
  or or_6 (or_5_out[1], d_latch_6_q, nor_1_out);
  or or_7 (or_5_out[2], d_latch_7_q, nor_1_out);
  or or_8 (or_8_out, d_latch_8_q, nor_1_out);
  or or_9 (or_9_out[0], d_latch_9_q, nor_2_out);
  or or_10 (or_9_out[1], d_latch_10_q, nor_2_out);
  or or_11 (or_9_out[2], d_latch_11_q, nor_2_out);
  or or_12 (or_12_out, d_latch_12_q, nor_2_out);
  or or_13 (or_13_out[0], d_latch_13_q, nor_3_out);
  or or_14 (or_13_out[1], d_latch_14_q, nor_3_out);
  or or_15 (or_13_out[2], d_latch_15_q, nor_3_out);
  or or_16 (or_16_out, d_latch_16_q, nor_3_out);
  or or_17 (or_17_out[0], d_latch_17_q, nor_4_out);
  or or_18 (or_17_out[1], d_latch_18_q, nor_4_out);
  or or_19 (or_17_out[2], d_latch_19_q, nor_4_out);
  or or_20 (or_20_out, d_latch_20_q, nor_4_out);
  not not_6 (not_6_out, out_35);
  not not_7 (not_7_out, out_39);
  not not_8 (not_8_out, out_43);
  not not_9 (not_9_out, out_47);
  nand nand_1 (out_33, or_20_out, not_6_out);
  nand nand_2 (out_34, out_33, not_6_out);
  Decoder #(.select(3), .disabled(0), .enable("false")) decoder_1 (
    .out0(DAC0[0]), .out1(DAC0[1]), .out2(DAC0[2]), .out3(DAC0[3]), .out4(DAC0[4]), .out5(DAC0[5]),
    .out6(DAC0[6]), .out7(DAC0[7]), .sel(or_17_out));
  nand nand_3 (out_37, or_16_out, not_7_out);
  nand nand_4 (out_38, out_37, not_7_out);
  Decoder #(.select(3), .disabled(0), .enable("false")) decoder_2 (
    .out0(DAC1[0]), .out1(DAC1[1]), .out2(DAC1[2]), .out3(DAC1[3]), .out4(DAC1[4]), .out5(DAC1[5]),
    .out6(DAC1[6]), .out7(DAC1[7]), .sel(or_13_out));
  nand nand_5 (out_41, or_12_out, not_8_out);
  nand nand_6 (out_42, out_41, not_8_out);
  Decoder #(.select(3), .disabled(0), .enable("false")) decoder_3 (
    .out0(DAC2[0]), .out1(DAC2[1]), .out2(DAC2[2]), .out3(DAC2[3]), .out4(DAC2[4]), .out5(DAC2[5]),
    .out6(DAC2[6]), .out7(DAC2[7]), .sel(or_9_out));
  nand nand_7 (out_45, or_8_out, not_9_out);
  nand nand_8 (out_46, out_45, not_9_out);
  Decoder #(.select(3), .disabled(0), .enable("false")) decoder_4 (
    .out0(DAC3[0]), .out1(DAC3[1]), .out2(DAC3[2]), .out3(DAC3[3]), .out4(DAC3[4]), .out5(DAC3[5]),
    .out6(DAC3[6]), .out7(DAC3[7]), .sel(or_5_out));
  Decoder #(.select(2), .disabled(0)) decoder_5 (
    .out0(out_49[0]), .out1(out_49[1]), .out2(out_49[2]), .out3(out_49[3]), .sel(undriven_17),
    .en(undriven_16));
  assign D0_2 = undriven_18 ? ~or_5_out[0] : 1'bz;  // Controlled_Inverter controlled_inverter_1
  assign D1_2 = undriven_18 ? ~or_5_out[1] : 1'bz;  // Controlled_Inverter controlled_inverter_2
  assign D2_2 = undriven_18 ? ~or_5_out[2] : 1'bz;  // Controlled_Inverter controlled_inverter_3
  assign D3_2 = undriven_18 ? ~or_8_out : 1'bz;  // Controlled_Inverter controlled_inverter_4
  assign D4_2 = undriven_19 ? ~or_9_out[0] : 1'bz;  // Controlled_Inverter controlled_inverter_5
  assign D5_2 = undriven_19 ? ~or_9_out[1] : 1'bz;  // Controlled_Inverter controlled_inverter_6
  assign D6_2 = undriven_19 ? ~or_9_out[2] : 1'bz;  // Controlled_Inverter controlled_inverter_7
  assign D7_2 = undriven_19 ? ~or_12_out : 1'bz;  // Controlled_Inverter controlled_inverter_8
  assign D8_2 = undriven_19 ? ~or_13_out[0] : 1'bz;  // Controlled_Inverter controlled_inverter_9
  assign D9_2 = undriven_19 ? ~or_13_out[1] : 1'bz;  // Controlled_Inverter controlled_inverter_10
  assign D10_2 = undriven_19 ? ~or_13_out[2] : 1'bz;  // Controlled_Inverter controlled_inverter_11
  assign D11_2 = undriven_19 ? ~or_16_out : 1'bz;  // Controlled_Inverter controlled_inverter_12
  assign D12_2 = undriven_19 ? ~or_17_out[0] : 1'bz;  // Controlled_Inverter controlled_inverter_13
  assign D13_2 = undriven_19 ? ~or_17_out[1] : 1'bz;  // Controlled_Inverter controlled_inverter_14
  assign D14_2 = undriven_19 ? ~or_17_out[2] : 1'bz;  // Controlled_Inverter controlled_inverter_15
  assign D15_2 = undriven_19 ? ~or_20_out : 1'bz;  // Controlled_Inverter controlled_inverter_16

  // Notes on the sheet:
  //   nTEST9QQ
  //   KEK3
  //   KEK2
  //   KEK1
  //   KEK0
endmodule

module D_LATCH (
  input  EN,
  input  D,
  output Q,
  output nQ
);

  D_Flip_Flop #(.trigger("high")) d_ff_1 (.clk(EN), .D(D), .Q(Q), .Qn(nQ));  // open: preset, en, reset
endmodule
